// Logisim project lastname_firstname.circ as structural Verilog
module main (
  input  in_1,
  input  in_2
);

  wire BEQ_Equal_bit, CLK, comparator_2_eq, comparator_3_eq, comparator_4_eq, comparator_5_eq,
       comparator_8_eq, comparator_9_eq, comparator_10_eq, Is_JALR, WrEn;
  wire [1:0] func;
  wire [2:0] comparator_6_eq;
  wire [3:0] DESTINATION, Destination_reg_q, EX_OP, ID_OP, ID_Rx_Code, ID_Ry_Code, MEM_OP, multiplexer_2_out,
       register_2_q, WB_OP_q;
  wire [19:0] ID_Off;
  wire [23:0] bit_extender_1_out, bit_extender_3_out;
  wire [31:0] A, adder_1_out, adder_2_out, adder_3_out, adder_5_out, Address, ALU_result, and_1_out, AT, B,
       BEQ_PC, bit_extender_2_out, DataToWrite, dual_ported_register_file_1_out2, EX_Off, EX_PC_q,
       EX_Result_q, FW_EX, ID_PC_q, LEA, LEA_q, Loaded_data, multiplexer_1_out, multiplexer_3_out, not_1_out,
       PC_q, ram_1_data, rom_1_data, Shift_Result;

  Register #(.width(32)) PC (.D(multiplexer_1_out), .Q(PC_q), .clk(CLK), .clr(in_2));  // open: en
  Bit_Extender #(.in_width(32), .out_width(24)) bit_extender_1 (.in(PC_q), .out(bit_extender_1_out));
  Adder #(.width(32)) adder_1 (.a(32'h1), .b(PC_q), .out(adder_1_out));  // open: cin, cout
  Clock clock_1 (.out(CLK));
  Multiplexer #(.select(2), .width(32)) multiplexer_1 (
    .in0(adder_1_out), .in1(AT), .in2(BEQ_PC), .out(multiplexer_1_out), .sel({BEQ_Equal_bit, Is_JALR}));  // open: in3, en
  ROM #(.addrWidth(24), .dataWidth(32)) rom_1 (.addr(bit_extender_1_out), .data(rom_1_data));  // open: sel
  Register #(.width(32)) Instruction_Reg (
    .D(rom_1_data), .en(1'b1), .Q({ID_OP, ID_Rx_Code, ID_Ry_Code, ID_Off}), .clk(CLK), .clr(Is_JALR));
  Register #(.width(32)) ID_PC (.D(PC_q), .Q(ID_PC_q), .clk(CLK));  // open: en, clr
  Adder #(.width(32)) adder_2 (.a(32'h1), .b(ID_PC_q), .out(adder_2_out));  // open: cin, cout
  Multiplexer #(.width(4)) multiplexer_2 (
    .in0(DESTINATION), .in1(4'b1111), .out(multiplexer_2_out), .sel(Is_JALR));  // open: en
  Multiplexer #(.width(32)) multiplexer_3 (
    .in0(DataToWrite), .in1(adder_2_out), .out(multiplexer_3_out), .sel(Is_JALR));  // open: en
  Comparator #(.width(4)) comparator_1 (.a(ID_OP), .b(4'b0100), .eq(Is_JALR));  // open: gt, lt
  Dual_Ported_Register_File dual_ported_register_file_1 (
    .CLK(CLK), .WrREGNO(multiplexer_2_out), .RdREGNO1(ID_Ry_Code), .RdREGNO2(ID_Off[3:0]),
    .INPUT(multiplexer_3_out), .OUT1(AT), .OUT2(dual_ported_register_file_1_out2), .WrEN(WrEn));
  assign bit_extender_2_out = {{12{1'b0}}, ID_Off};  // Bit_Extender bit_extender_2
  Register #(.width(32)) register_1 (.D(bit_extender_2_out), .Q(EX_Off), .clk(CLK));  // open: en, clr
  Register #(.width(4)) register_2 (.D(ID_Rx_Code), .Q(register_2_q), .clk(CLK));  // open: en, clr
  Register #(.width(32)) Reg_A (.D(AT), .Q(B), .clk(CLK));  // open: en, clr
  Register #(.width(32)) Reg_B (.D(dual_ported_register_file_1_out2), .Q(A));  // open: en, clk, clr
  Register #(.width(4)) u_EX_OP (.D(ID_OP), .Q(EX_OP), .clk(CLK));  // open: en, clr
  Register #(.width(32)) EX_PC (.D(ID_PC_q), .Q(EX_PC_q), .clk(CLK));  // open: en, clr
  Comparator #(.width(32)) comparator_2 (.a(A), .b(B), .eq(comparator_2_eq));  // open: gt, lt
  Comparator #(.width(4)) comparator_3 (.a(EX_OP), .b(4'b1000), .eq(comparator_3_eq));  // open: gt, lt
  Adder #(.width(32)) adder_3 (.a(B), .b(A), .out(adder_3_out));  // open: cin, cout
  assign and_1_out = A & B;  // AND_Gate and_1, 32 bits wide
  Adder #(.width(32)) adder_4 (.a(EX_PC_q), .b(EX_Off), .out(BEQ_PC));  // open: cin, cout
  Adder #(.width(32)) adder_5 (.a(B), .b(EX_Off), .out(adder_5_out));  // open: cin, cout
  assign not_1_out = ~and_1_out;  // NOT_Gate not_1, 32 bits wide
  Comparator #(.width(4)) comparator_4 (.a(EX_OP), .b(4'b0011), .eq(comparator_4_eq));  // open: gt, lt
  Multiplexer #(.width(2)) multiplexer_4 (
    .in0(EX_OP[1:0]), .in1(2'b11), .out(func), .sel(comparator_3_eq));  // open: en
  and and_2 (BEQ_Equal_bit, comparator_2_eq, comparator_4_eq);
  Multiplexer #(.select(2), .width(32)) multiplexer_5 (
    .in0(adder_3_out), .in1(adder_5_out), .in2(not_1_out), .in3(Shift_Result), .out(FW_EX), .sel(func));  // open: en
  Register #(.width(4)) Destination_reg (.D(register_2_q), .Q(Destination_reg_q), .clk(CLK));  // open: en, clr
  Register #(.width(32)) EX_Result (.D(FW_EX), .Q(EX_Result_q), .clk(CLK));  // open: en, clr
  Register #(.width(4)) register_3 (.D(EX_OP), .Q(MEM_OP), .clk(CLK));  // open: en, clr
  Register #(.width(32)) LDR_Addr (.D(adder_5_out), .Q(Address), .clk(CLK));  // open: en, clr
  Register #(.width(32)) u_LEA (.D(BEQ_PC), .Q(LEA_q), .clk(CLK));  // open: en, clr
  Bit_Extender #(.in_width(32), .out_width(24)) bit_extender_3 (.in(Address), .out(bit_extender_3_out));
  Comparator #(.width(4)) comparator_5 (.a(MEM_OP), .b(4'b0111), .eq(comparator_5_eq));  // open: gt, lt
  RAM #(.addrWidth(24), .dataWidth(32), .bus("separate")) ram_1 (
    .addr(bit_extender_3_out), .din(EX_Result_q), .data(ram_1_data), .str(comparator_5_eq), .ld(in_1));  // open: sel, clk, clr
  Register #(.width(4)) WB_Dest_reg (.D(Destination_reg_q), .Q(DESTINATION), .clk(CLK));  // open: en, clr
  Register #(.width(32)) u_Loaded_Data (.D(ram_1_data), .Q(Loaded_data), .clk(CLK));  // open: en, clr
  Register #(.width(4)) WB_OP (.D(MEM_OP), .Q(WB_OP_q), .clk(CLK));  // open: en, clr
  Register #(.width(32)) u_ALU_result (.D(EX_Result_q), .Q(ALU_result), .clk(CLK));  // open: en, clr
  Register #(.width(32)) LEA_2 (.D(LEA_q), .Q(LEA), .clk(CLK));  // open: en, clr
  Comparator #(.width(4)) comparator_6 (.a(WB_OP_q), .b(4'b0110), .eq(comparator_6_eq[0]));  // open: gt, lt
  Comparator #(.width(4)) comparator_7 (.a(WB_OP_q), .b(4'b0101), .eq(comparator_6_eq[1]));  // open: gt, lt
  Comparator #(.width(4)) comparator_8 (.a(WB_OP_q), .b(4'b0000), .eq(comparator_8_eq));  // open: gt, lt
  Comparator #(.width(4)) comparator_9 (.a(WB_OP_q), .b(4'b0001), .eq(comparator_9_eq));  // open: gt, lt
  Comparator #(.width(4)) comparator_10 (.a(WB_OP_q), .b(4'b0010), .eq(comparator_10_eq));  // open: gt, lt
  or or_1 (comparator_6_eq[2], comparator_8_eq, comparator_9_eq, comparator_10_eq);
  or or_2 (WrEn, comparator_6_eq[2], comparator_6_eq[1], comparator_6_eq[0]);
  Multiplexer #(.select(3), .width(32)) multiplexer_6 (
    .in1(LEA), .in2(Loaded_data), .in4(ALU_result), .out(DataToWrite), .sel(comparator_6_eq));  // open: in0, in3, in5, in6, in7, en

  // Other names for the same wires on the sheet: ID_Rz_Code[3:0] = ID_Off[3:0]

  // Notes on the sheet:
  //   contents of rom_1 (hex, n*v repeats v):
  //   19000005 1a000006 ba00009 6*7b900000
endmodule

module Dual_Ported_Register_File (
  input  CLK,
  input  WrEN,
  input  [3:0] WrREGNO,
  input  [3:0] RdREGNO1,
  input  [3:0] RdREGNO2,
  input  [31:0] INPUT,
  output [31:0] OUT1,
  output [31:0] OUT2
);

  wire En_a0, En_a1, En_a2, En_at, En_fp, En_k0, En_ra, En_s0, En_s1, En_s2, En_sp, En_t0, En_t1, En_t2,
       En_v0;
  wire [31:0] a0, a1, a2, at, fp, k0, ra, s0, s1, s2, sp, t0, t1, t2, v0, zero;

  Decoder #(.select(4), .disabled(0)) decoder_1 (
    .out1(En_at), .out2(En_v0), .out3(En_a0), .out4(En_a1), .out5(En_a2), .out6(En_t0), .out7(En_t1),
    .out8(En_t2), .out9(En_s0), .out10(En_s1), .out11(En_s2), .out12(En_k0), .out13(En_sp), .out14(En_fp),
    .out15(En_ra), .sel(WrREGNO), .en(WrEN));  // open: out0
  Register #(.width(32)) u_zero (.D(INPUT), .en(1'b0), .Q(zero), .clk(CLK));  // open: clr
  Register #(.width(32)) u_at (.D(INPUT), .en(En_at), .Q(at), .clk(CLK));  // open: clr
  Register #(.width(32)) u_v0 (.D(INPUT), .en(En_v0), .Q(v0), .clk(CLK));  // open: clr
  Register #(.width(32)) u_a0 (.D(INPUT), .en(En_a0), .Q(a0), .clk(CLK));  // open: clr
  Register #(.width(32)) u_a1 (.D(INPUT), .en(En_a1), .Q(a1), .clk(CLK));  // open: clr
  Register #(.width(32)) u_a2 (.D(INPUT), .en(En_a2), .Q(a2), .clk(CLK));  // open: clr
  Register #(.width(32)) u_t0 (.D(INPUT), .en(En_t0), .Q(t0), .clk(CLK));  // open: clr
  Register #(.width(32)) u_t1 (.D(INPUT), .en(En_t1), .Q(t1), .clk(CLK));  // open: clr
  Multiplexer #(.select(4), .width(32), .disabled(0), .enable("false")) multiplexer_1 (
    .in0(zero), .in1(at), .in2(v0), .in3(a0), .in4(a1), .in5(a2), .in6(t0), .in7(t1), .in8(t2), .in9(s0),
    .in10(s1), .in11(s2), .in12(k0), .in13(sp), .in14(fp), .in15(ra), .out(OUT2), .sel(RdREGNO2));
  Register #(.width(32)) u_t2 (.D(INPUT), .en(En_t2), .Q(t2), .clk(CLK));  // open: clr
  Register #(.width(32)) u_s0 (.D(INPUT), .en(En_s0), .Q(s0), .clk(CLK));  // open: clr
  Register #(.width(32)) u_s1 (.D(INPUT), .en(En_s1), .Q(s1), .clk(CLK));  // open: clr
  Register #(.width(32)) u_s2 (.D(INPUT), .en(En_s2), .Q(s2), .clk(CLK));  // open: clr
  Register #(.width(32)) u_k0 (.D(INPUT), .en(En_k0), .Q(k0), .clk(CLK));  // open: clr
  Register #(.width(32)) u_sp (.D(INPUT), .en(En_sp), .Q(sp), .clk(CLK));  // open: clr
  Register #(.width(32)) u_fp (.D(INPUT), .en(En_fp), .Q(fp), .clk(CLK));  // open: clr
  Register #(.width(32)) u_ra (.D(INPUT), .en(En_ra), .Q(ra), .clk(CLK));  // open: clr
  Multiplexer #(.select(4), .width(32), .disabled(0), .enable("false")) multiplexer_2 (
    .in0(zero), .in1(at), .in2(v0), .in3(a0), .in4(a1), .in5(a2), .in6(t0), .in7(t1), .in8(t2), .in9(s0),
    .in10(s1), .in11(s2), .in12(k0), .in13(sp), .in14(fp), .in15(ra), .out(OUT1), .sel(RdREGNO1));

  // Notes on the sheet:
  //   MODIFY AT YOUR OWN RISK
endmodule
